# Fritzing sketch mkr1010-wiring (saved by Fritzing 0.9.9b)
breadboards: 1

parts:
  R1 = Resistor [tolerance=±5% resistance=220 power=0.25 package=THT]
  Part1 = Arduino MKR1000
  SHT1 = SHT3X [package="SIP (Single Inline) [THT]"]
  LED2 = LED - 5mm [color="Red (633nm)" current=0.030 package="5 mm [THT]"]

nets:
  N1: R1.Pin_0, Part1.GND, SHT1.SCL
  N2: R1.Pin_1, LED2.cathode
  N3: Part1.D6, LED2.anode
  N4: Part1.D11_SDA, SHT1.GND
  N5: Part1.D12_SCL, SHT1.SDA
  VCC: Part1.VCC, SHT1.VDD

custom parts:
  Arduino MKR1000: MKR1000 is a powerful board that combines the functionality of the Zero and the Wi-Fi Shield. It is the ideal solution for makers wanting to design IoT projects with minimal previous experience in networking
  SHT3X: Breadboard Only. Copied from TSYS01
