# Fritzing sketch wiring (saved by Fritzing 0.9.9b)
breadboards: 1

parts:
  Part1 = Arduino Nano 33 IOT
  LED1 = LED - 5mm [color="Red (633nm)" current=0.030 package="5 mm [THT]"]
  R2 = Resistor [tolerance=±5% resistance=220 power=0.25 package=THT]
  SHT1 = SHT3X [package="SIP (Single Inline) [THT]"]

nets:
  N1: Part1.RESET, Part1.A7
  N2: Part1.GND, Part1.D13~, LED1.anode, R2.Pin_1, SHT1.SCL
  N3: Part1.D11/MOSI, Part1.+5V
  N4: Part1.A5, SHT1.SDA
  N5: Part1.A4, SHT1.GND
  3V3: Part1.3V3, SHT1.VDD
  N6: LED1.cathode, R2.Pin_0

custom parts:
  Arduino Nano 33 IOT: The Arduino Nano 33 IoT is the easiest and cheapest point of entry to enhance existing devices (and creating new ones) to be part of the IoT and designing pico-network applications. Whether you are looking at building a sensor network connected to your office or home router, or if you want to create a BLE device sending data to a cellphone, the Nano 33 IoT is your one-stop-solution for many of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
  SHT3X: Breadboard Only. Copied from TSYS01
