# Fritzing sketch wiring (saved by Fritzing 0.9.3b)
breadboards: 1

parts:
  R1 = Resistor [tolerance=±5% resistance=220 package=THT]
  Part1 = Arduino MKR1000
  RHT1 = Humidity and Temperature Sensor RHT03
  LED1 = smd LED [color="Red (633nm)" package="1206 [SMD]"]
  R2 = Resistor [tolerance=±5% resistance=10k package="0805 [SMD]"]

nets:
  N1: R1.Pin_0, LED1.cathode
  N2: R1.Pin_1, Part1.GND, RHT1.GND_2
  N3: Part1.D6, LED1.anode
  N4: Part1.D7, RHT1.Data-signal, R2.Pin_0
  VCC: Part1.VCC, RHT1.Vcc, R2.Pin_1

custom parts:
  Arduino MKR1000: MKR1000 is a powerful board that combines the functionality of the Zero and the Wi-Fi Shield. It is the ideal solution for makers wanting to design IoT projects with minimal previous experience in networking
