# Fritzing sketch rpi-sht31 (saved by Fritzing 0.9.9b)
breadboards: 1

parts:
  Raspberry_Pi1 = Raspberry Pi 2
  SHT1 = SHT3X [package="SIP (Single Inline) [THT]"]
  LED1 = smd LED [color="Red (633nm)" package="0603 [SMD]"]
  R1 = Resistor [tolerance=±5% resistance=220 package="0805 [SMD]"]

nets:
  3V3: Raspberry_Pi1.3v3, SHT1.VDD
  N1: Raspberry_Pi1.GPIO2, SHT1.GND
  N2: Raspberry_Pi1.GPIO3, SHT1.SDA
  N3: Raspberry_Pi1.GND, SHT1.SCL, R1.Pin_0
  N4: Raspberry_Pi1.GPIO18, LED1.anode
  N5: LED1.cathode, R1.Pin_1

custom parts:
  SHT3X: Breadboard Only. Copied from TSYS01
